# Fritzing sketch schematics (saved by Fritzing 0.9.2b)

parts:
  NEOPIXEL1 = Neopixel Strip -- White (60/m)
  Composant1 = Arduino Nano (Rev3.0)
  U1 = LIPO-2000mAh [package=lipo-2000]

nets:
  N1: NEOPIXEL1.+5V, Composant1.D6
  N2: NEOPIXEL1.DI, Composant1.5V
  GND: NEOPIXEL1.GND, Composant1.GND, U1.-
  N3: Composant1.VIN, U1.+

notes:
  MKR1000

custom parts:
  Neopixel Strip -- White (60/m): Neopixel Strip, White, 60 pixels per meter.
